// Logisim project add 32 bit.circ as structural Verilog: 4 circuits, main circuit main
module main (
  input  ci,
  input  [31:0] a,
  input  [31:0] b,
  output ci_1,
  output [31:0] si
);

  wire main_1_ci_1, main_2_ci_1, main_3_ci_1;

  adder_8_bit_main main_1 (.ci(ci), .a(a[7:0]), .b(b[7:0]), .out_4(si[7:0]), .ci_1(main_1_ci_1));
  adder_8_bit_main main_2 (.ci(main_1_ci_1), .a(a[15:8]), .b(b[15:8]), .out_4(si[15:8]), .ci_1(main_2_ci_1));
  adder_8_bit_main main_3 (.ci(main_2_ci_1), .a(a[23:16]), .b(b[23:16]), .out_4(si[23:16]), .ci_1(main_3_ci_1));
  adder_8_bit_main main_4 (.ci(main_3_ci_1), .a(a[31:24]), .b(b[31:24]), .out_4(si[31:24]), .ci_1(ci_1));
endmodule

module _1 (
  input  ci,
  input  a,
  input  b,
  output si,
  output ci_1
);

  wire and_1_out, and_2_out, and_3_out, not_1_out, not_2_out, or_1_out, or_3_out;

  or or_1 (or_1_out, a, b);
  and and_1 (and_1_out, a, b);
  not not_1 (not_1_out, and_1_out);
  and and_2 (and_2_out, or_1_out, not_1_out);
  or or_2 (ci_1, and_3_out, and_1_out);
  and and_3 (and_3_out, ci, and_2_out);
  or or_3 (or_3_out, ci, and_2_out);
  not not_2 (not_2_out, and_3_out);
  and and_4 (si, not_2_out, or_3_out);
endmodule

module adder_8_bit (
  input  ci,
  input  [7:0] a,
  input  [7:0] b,
  output [7:0] out_4,
  output ci_1
);

  wire adder_1_bit_1_ci_1, adder_1_bit_2_ci_1, adder_1_bit_3_ci_1, adder_1_bit_4_ci_1, adder_1_bit_5_ci_1,
       adder_1_bit_6_ci_1, adder_1_bit_7_ci_1;

  adder_8_bit_adder_1_bit adder_1_bit_1 (.ci(ci), .a(a[0]), .b(b[0]), .si(out_4[0]), .ci_1(adder_1_bit_1_ci_1));
  adder_8_bit_adder_1_bit adder_1_bit_2 (
    .ci(adder_1_bit_1_ci_1), .a(a[1]), .b(b[1]), .si(out_4[1]), .ci_1(adder_1_bit_2_ci_1));
  adder_8_bit_adder_1_bit adder_1_bit_3 (
    .ci(adder_1_bit_2_ci_1), .a(a[2]), .b(b[2]), .si(out_4[2]), .ci_1(adder_1_bit_3_ci_1));
  adder_8_bit_adder_1_bit adder_1_bit_4 (
    .ci(adder_1_bit_3_ci_1), .a(a[3]), .b(b[3]), .si(out_4[3]), .ci_1(adder_1_bit_4_ci_1));
  adder_8_bit_adder_1_bit adder_1_bit_5 (
    .ci(adder_1_bit_4_ci_1), .a(a[4]), .b(b[4]), .si(out_4[4]), .ci_1(adder_1_bit_5_ci_1));
  adder_8_bit_adder_1_bit adder_1_bit_6 (
    .ci(adder_1_bit_5_ci_1), .a(a[5]), .b(b[5]), .si(out_4[5]), .ci_1(adder_1_bit_6_ci_1));
  adder_8_bit_adder_1_bit adder_1_bit_7 (
    .ci(adder_1_bit_6_ci_1), .a(a[6]), .b(b[6]), .si(out_4[6]), .ci_1(adder_1_bit_7_ci_1));
  adder_8_bit_adder_1_bit adder_1_bit_8 (.ci(adder_1_bit_7_ci_1), .a(a[7]), .b(b[7]), .si(out_4[7]), .ci_1(ci_1));
endmodule

module adder_1_bit (
  input  ci,
  input  a,
  input  b,
  output si,
  output ci_1
);

  wire and_1_out, and_2_out, and_3_out, not_1_out, not_2_out, or_1_out, or_3_out;

  or or_1 (or_1_out, a, b);
  and and_1 (and_1_out, a, b);
  not not_1 (not_1_out, and_1_out);
  and and_2 (and_2_out, or_1_out, not_1_out);
  or or_2 (ci_1, and_3_out, and_1_out);
  and and_3 (and_3_out, ci, and_2_out);
  or or_3 (or_3_out, ci, and_2_out);
  not not_2 (not_2_out, and_3_out);
  and and_4 (si, not_2_out, or_3_out);
endmodule
