// Logisim project control.circ as structural Verilog: 1 circuit, main circuit main
module main (
  input  clock,
  input  start,
  input  rep32,
  input  restart,
  input  do_add,
  input  do_shift,
  output product_clear,
  output select_mulitpier,
  output load_register,
  output clear,
  output add
);

  wire and_1_out, and_2_out, and_3_out, and_4_out, and_5_out, and_6_out, and_7_out, and_9_out, and_10_out,
       and_12_out, and_13_out, not_1_out, not_2_out, not_3_out, not_4_out, not_5_out, not_6_out, not_7_out;
  wire [2:0] or_3_out, register_1_q;

  not not_1 (not_1_out, rep32);
  not not_2 (not_2_out, restart);
  not not_3 (not_3_out, do_add);
  not not_4 (not_4_out, do_shift);
  Register #(.width(3)) register_1 (.D(or_3_out), .Q(register_1_q), .clk(clock));  // open: en, clr
  not not_5 (not_5_out, register_1_q[0]);
  not not_6 (not_6_out, register_1_q[1]);
  not not_7 (not_7_out, register_1_q[2]);
  and and_1 (and_1_out, not_7_out, register_1_q[1], register_1_q[0], rep32);
  and and_2 (and_2_out, register_1_q[2], not_6_out, not_5_out, not_2_out);
  and and_3 (and_3_out, not_7_out, not_6_out, register_1_q[0], do_add, not_4_out);
  and and_4 (and_4_out, not_7_out, not_6_out, register_1_q[0], not_3_out, do_shift);
  and and_5 (and_5_out, not_7_out, register_1_q[1], not_5_out);
  and and_6 (and_6_out, not_7_out, not_6_out, register_1_q[0], not_3_out, do_shift);
  and and_7 (and_7_out, not_7_out, register_1_q[1], not_5_out);
  and and_8 (select_mulitpier, register_1_q[1], not_7_out, register_1_q[0]);
  and and_9 (and_9_out, not_7_out, not_6_out, not_5_out, start);
  and and_10 (and_10_out, not_7_out, register_1_q[1], register_1_q[0], not_1_out);
  and and_11 (product_clear, not_5_out, not_6_out, not_7_out);
  and and_12 (and_12_out, not_5_out, not_7_out, not_6_out);
  or or_1 (or_3_out[2], and_1_out, and_2_out);
  and and_13 (and_13_out, register_1_q[1], not_7_out, register_1_q[0]);
  or or_2 (or_3_out[1], and_3_out, and_4_out, and_5_out);
  or or_3 (or_3_out[0], and_9_out, and_6_out, and_7_out, and_10_out);
  or or_4 (load_register, and_12_out, and_13_out);
  and and_14 (clear, register_1_q[2], not_5_out, not_6_out);
  and and_15 (add, not_5_out, register_1_q[1], not_7_out);
endmodule
