// Logisim project datapath.circ as structural Verilog: 2 circuits, main circuit main
module main (
  input  [31:0] multipilier,
  input  slect_input_mulplr,
  input  [31:0] multipicant,
  input  load_input_multip,
  input  add,
  input  clock,
  input  clear,
  input  product_clear,
  output [31:0] result_multipler,
  output do_add,
  output do_shift,
  output [31:0] result_product,
  output rep_32
);

  wire or_1_out, or_2_out;
  wire [7:0] counter_1_q;
  wire [31:0] adder_32_bit_si, multipicant_q, multiplexer_1_out, multiplexer_2_out, shifter_multipler_2,
       shifter_product_2;

  Multiplexer #(.width(32)) multiplexer_1 (
    .in0(multipilier), .in1(shifter_multipler_2), .out(multiplexer_1_out), .sel(slect_input_mulplr));  // open: en
  Register #(.width(32)) u_multipicant (.D(multipicant), .Q(multipicant_q), .clk(clock));  // open: en, clr
  Counter #(.max('h20), .ongoal("stay")) counter_1 (
    .Q(counter_1_q), .clk(slect_input_mulplr), .clr(clear));  // open: load, D, count, carry
  Register #(.width(32)) multiplier (
    .D(multiplexer_1_out), .en(load_input_multip), .Q(result_multipler), .clk(clock));  // open: clr
  or or_1 (or_1_out, slect_input_mulplr, add);
  Register #(.width(32)) product_reg (
    .D(multiplexer_2_out), .en(or_1_out), .Q(result_product), .clk(clock), .clr(product_clear));
  Comparator comparator_1 (.a(counter_1_q), .b(8'h20), .eq(rep_32));  // open: gt, lt
  and and_1 (do_add, result_multipler[0], 1'b1);
  add_32_bit_main adder_32_bit (.ci(1'b0), .a(multipicant_q), .b(result_product), .si(adder_32_bit_si));  // open: ci_1
  Multiplexer #(.width(32)) multiplexer_2 (
    .in0(adder_32_bit_si), .in1(shifter_product_2), .out(multiplexer_2_out), .sel(slect_input_mulplr));  // open: en
  or or_2 (or_2_out, result_multipler[0], 1'b0);
  not not_1 (do_shift, or_2_out);
  sshifter_main shifter (
    .multipler(result_multipler), .product(result_product), .multipler_2(shifter_multipler_2),
    .product_2(shifter_product_2));
endmodule

module adder_1bit (
  input  ci,
  input  a,
  input  b,
  output si,
  output ci_1
);

  wire and_1_out, and_2_out, and_3_out, not_1_out, not_2_out, or_1_out, or_3_out;

  or or_1 (or_1_out, a, b);
  and and_1 (and_1_out, a, b);
  not not_1 (not_1_out, and_1_out);
  and and_2 (and_2_out, or_1_out, not_1_out);
  or or_2 (ci_1, and_3_out, and_1_out);
  and and_3 (and_3_out, ci, and_2_out);
  or or_3 (or_3_out, ci, and_2_out);
  not not_2 (not_2_out, and_3_out);
  and and_4 (si, not_2_out, or_3_out);
endmodule
