// Logisim project mult32.circ as structural Verilog: 1 circuit, main circuit main
module main (
  input  [31:0] Multiplier,
  input  [31:0] Multipicant,
  output [31:0] Result_Of_First_32,
  output [31:0] Result_Of_Last_32
);

  wire clock_1_out, main_1_add, main_1_clear, main_1_load_register, main_1_product_clear,
       main_1_select_mulitpier, main_2_do_add, main_2_do_shift, main_2_rep_32, Restart_out, Start_out;

  Button Restart (.out(Restart_out));
  Clock clock_1 (.out(clock_1_out));
  Button Start (.out(Start_out));
  control_main main_1 (
    .clock(clock_1_out), .start(Start_out), .rep32(main_2_rep_32), .restart(Restart_out),
    .do_add(main_2_do_add), .do_shift(main_2_do_shift), .product_clear(main_1_product_clear),
    .select_mulitpier(main_1_select_mulitpier), .load_register(main_1_load_register), .clear(main_1_clear),
    .add(main_1_add));
  datapath_main main_2 (
    .multipilier(Multiplier), .slect_input_mulplr(main_1_select_mulitpier), .multipicant(Multipicant),
    .load_input_multip(main_1_load_register), .add(main_1_add), .clock(clock_1_out), .clear(main_1_clear),
    .product_clear(main_1_product_clear), .result_multipler(Result_Of_First_32), .do_add(main_2_do_add),
    .do_shift(main_2_do_shift), .result_product(Result_Of_Last_32), .rep_32(main_2_rep_32));
endmodule
