// Logisim project sshifter.circ as structural Verilog: 1 circuit, main circuit main
module main (
  input  [31:0] multipler,
  input  [31:0] product,
  output [31:0] multipler_2,
  output [31:0] product_2
);


  assign multipler_2 = {product[0], multipler[31:1]};
  assign product_2 = {1'b0, product[31:1]};
endmodule
